// Logisim project lab11.circ as structural Verilog
module Ex1 (
  input  [7:0] in,
  output Out1,
  output [7:0] Out2
);

  not not_1 (Out2[7], in[7]);
  and and_1 (Out1, in[0], in[7]);

  assign Out2[6:0] = in[6:0];
endmodule

module rotr (
  input  [15:0] A,
  input  [3:0] B,
  output [15:0] out_3
);

  wire [15:0] multiplexer_1_out, multiplexer_2_out, multiplexer_3_out, shift1_1_out_2, shift2_1_out_2,
       shift4_1_out_2, shift8_1_out_2;

  shift1 shift1_1 (.in_1(A), .out_2(shift1_1_out_2));
  Multiplexer #(.width(16)) multiplexer_1 (
    .in0(A), .in1(shift1_1_out_2), .out(multiplexer_1_out), .sel(B[0]));  // open: en
  Multiplexer #(.width(16)) multiplexer_2 (
    .in0(multiplexer_1_out), .in1(shift2_1_out_2), .out(multiplexer_2_out), .sel(B[1]));  // open: en
  shift2 shift2_1 (.in_1(multiplexer_1_out), .out_2(shift2_1_out_2));
  shift4 shift4_1 (.in_1(multiplexer_2_out), .out_2(shift4_1_out_2));
  Multiplexer #(.width(16)) multiplexer_3 (
    .in0(multiplexer_2_out), .in1(shift4_1_out_2), .out(multiplexer_3_out), .sel(B[2]));  // open: en
  shift8 shift8_1 (.in_1(multiplexer_3_out), .out_2(shift8_1_out_2));
  Multiplexer #(.width(16)) multiplexer_4 (
    .in0(multiplexer_3_out), .in1(shift8_1_out_2), .out(out_3), .sel(B[3]));  // open: en
endmodule

module shift1 (
  input  [15:0] in_1,
  output [15:0] out_2
);


  assign out_2 = {in_1[0], in_1[15:1]};
endmodule

module shift2 (
  input  [15:0] in_1,
  output [15:0] out_2
);


  assign out_2 = {in_1[1:0], in_1[15:2]};
endmodule

module shift4 (
  input  [15:0] in_1,
  output [15:0] out_2
);


  assign out_2 = {in_1[3:0], in_1[15:4]};
endmodule

module shift8 (
  input  [15:0] in_1,
  output [15:0] out_2
);


  assign out_2 = {in_1[7:0], in_1[15:8]};
endmodule

module fib (
);

  wire clock_1_out, comparator_1_lt, not_1_out, register_1_q;
  wire [7:0] counter_1_q;
  wire [15:0] adder_1_out, multiplexer_1_out, multiplexer_2_out, multiplexer_3_out, register_2_q,
       register_3_q;

  Register #(.width(1)) register_1 (.D(1'b1), .Q(register_1_q), .clk(clock_1_out));  // open: en, clr
  Clock clock_1 (.out(clock_1_out));
  Multiplexer #(.width(16)) multiplexer_1 (
    .in0(16'h1), .in1(adder_1_out), .out(multiplexer_1_out), .sel(register_1_q));  // open: en
  Multiplexer #(.width(16)) multiplexer_2 (
    .in0(multiplexer_1_out), .out(multiplexer_2_out), .sel(not_1_out));  // open: in1, en
  Counter counter_1 (.Q(counter_1_q), .clk(clock_1_out));  // open: load, D, count, carry, clr
  Register #(.width(16)) register_2 (.D(multiplexer_2_out), .Q(register_2_q), .clk(clock_1_out));  // open: en, clr
  Multiplexer #(.width(16)) multiplexer_3 (
    .in0(register_2_q), .in1({16{1'b0}}), .out(multiplexer_3_out), .sel(not_1_out));  // open: en
  Register #(.width(16)) register_3 (.D(multiplexer_3_out), .Q(register_3_q), .clk(clock_1_out));  // open: en, clr
  Comparator #(.mode("unsigned")) comparator_1 (.a(counter_1_q), .b(8'hf), .lt(comparator_1_lt));  // open: gt, eq
  Adder #(.width(16)) adder_1 (.a(register_2_q), .b(register_3_q), .out(adder_1_out));  // open: cin, cout
  not not_1 (not_1_out, comparator_1_lt);
  // Probe on adder_1_out
endmodule
