// Logisim project lab12ALU.circ as structural Verilog: 1 circuit, main circuit ALU
// LAB12-ALU
module ALU (
  input  [31:0] ALU_Source_1,
  input  [31:0] ALU_Source_2,
  input  [2:0] ALU_Control,
  output [31:0] ALU_Result
);

  wire [4:0] s25;
  wire [31:0] \and , multiplexer_1_out, multiplexer_2_out, multiplexer_3_out, multiplexer_4_out,
       multiplexer_5_out, multiplexer_7_out, \or , rl, rr, sll, sra, srl, \xor ;

  // Probe on ALU_Source_1
  // Probe on ALU_Source_2
  assign \and  = ALU_Source_1 & ALU_Source_2;  // AND_Gate and_1, 32 bits wide
  assign \or  = ALU_Source_1 | ALU_Source_2;  // OR_Gate or_1, 32 bits wide
  assign \xor  = ALU_Source_1 ^ ALU_Source_2;  // XOR_Gate xor_1, 32 bits wide
  Shifter #(.width(32)) shifter_1 (.in(ALU_Source_1), .\dist (s25), .out(sll));
  Shifter #(.width(32), .shift("lr")) shifter_2 (.in(ALU_Source_1), .\dist (s25), .out(srl));
  Shifter #(.width(32), .shift("ar")) shifter_3 (.in(ALU_Source_1), .\dist (s25), .out(sra));
  Shifter #(.width(32), .shift("rl")) shifter_4 (.in(ALU_Source_1), .\dist (s25), .out(rl));
  Shifter #(.width(32), .shift("rr")) shifter_5 (.in(ALU_Source_1), .\dist (s25), .out(rr));
  Bit_Extender #(.in_width(32), .out_width(5)) bit_extender_1 (.in(ALU_Source_2), .out(s25));
  // Probe on ALU_Result
  Multiplexer #(.width(32)) multiplexer_1 (
    .in0(sll), .in1(srl), .out(multiplexer_1_out), .sel(ALU_Control[0]));  // open: en
  Multiplexer #(.width(32)) multiplexer_2 (
    .in0(sra), .in1(rl), .out(multiplexer_2_out), .sel(ALU_Control[0]));  // open: en
  Multiplexer #(.width(32)) multiplexer_3 (
    .in0(rr), .in1(\and ), .out(multiplexer_3_out), .sel(ALU_Control[0]));  // open: en
  Multiplexer #(.width(32)) multiplexer_4 (
    .in0(\or ), .in1(\xor ), .out(multiplexer_4_out), .sel(ALU_Control[0]));  // open: en
  Multiplexer #(.width(32)) multiplexer_5 (
    .in0(multiplexer_1_out), .in1(multiplexer_2_out), .out(multiplexer_5_out), .sel(ALU_Control[1]));  // open: en
  Multiplexer #(.width(32)) multiplexer_6 (
    .in0(multiplexer_5_out), .in1(multiplexer_7_out), .out(ALU_Result), .sel(ALU_Control[2]));  // open: en
  Multiplexer #(.width(32)) multiplexer_7 (
    .in0(multiplexer_3_out), .in1(multiplexer_4_out), .out(multiplexer_7_out), .sel(ALU_Control[1]));  // open: en

  // Other names for the same wires on the sheet: control[2:0] = ALU_Control; result[31:0] = ALU_Result;
  //   source1[31:0] = ALU_Source_1; source2[31:0] = ALU_Source_2

  // Notes on the sheet:
  //   DO NOT CROSS WIRES
  //   OVER THIS BOX
  //   DO NOT CROSS WIRES
  //   OVER THIS BOX
  //   COMPUTE ALL POSSIBLE OPERATIONS
  //   DO NOT CROSS WIRES
  //   OVER THIS BOX
  //   DO NOT CROSS WIRES
  //   OVER THIS BOX
  //   SELECT THE REQUESTED RESULT
  //   oh wait i can use a single MUX
endmodule
