// Logisim project lab12Regfile.circ as structural Verilog: 1 circuit, main circuit main
// CPU
module main (
  input  [1:0] RS,
  input  [1:0] RT,
  input  [1:0] RD,
  input  [7:0] RD_WRITE_VALUE,
  input  RD_WRITE_ENABLE,
  output [7:0] RS_READ_VALUE,
  output [7:0] RT_READ_VALUE,
  output [7:0] REG_0_VALUE,
  output [7:0] REG_1_VALUE,
  output [7:0] REG_2_VALUE,
  output [7:0] REG_3_VALUE
);

  wire clk, write1, write2, write3;
  wire [7:0] multiplexer_1_out, multiplexer_3_out, multiplexer_4_out, multiplexer_5_out, multiplexer_6_out,
       multiplexer_8_out, multiplexer_9_out, r1in, r2in, r3in;

  Clock CLOCK (.out(clk));
  Demultiplexer #(.select(2), .width(8)) demultiplexer_1 (
    .out1(r1in), .out2(r2in), .out3(r3in), .in(RD_WRITE_VALUE), .sel(RD));  // open: out0, en
  Register Reg_0 (.D({8{1'b0}}), .Q(REG_0_VALUE), .clk(clk));  // open: en, clr
  Multiplexer #(.width(8)) multiplexer_1 (
    .in0(REG_0_VALUE), .in1(REG_1_VALUE), .out(multiplexer_1_out), .sel(RS[0]));  // open: en
  Multiplexer #(.width(8)) multiplexer_2 (
    .in0(multiplexer_1_out), .in1(multiplexer_3_out), .out(RS_READ_VALUE), .sel(RS[1]));  // open: en
  Multiplexer #(.width(8)) multiplexer_3 (
    .in0(REG_2_VALUE), .in1(REG_3_VALUE), .out(multiplexer_3_out), .sel(RS[0]));  // open: en
  Multiplexer #(.width(8)) multiplexer_4 (
    .in0(REG_0_VALUE), .in1(REG_1_VALUE), .out(multiplexer_4_out), .sel(RT[0]));  // open: en
  Multiplexer #(.width(8)) multiplexer_5 (
    .in0(REG_2_VALUE), .in1(REG_3_VALUE), .out(multiplexer_5_out), .sel(RT[0]));  // open: en
  Demultiplexer #(.select(2)) demultiplexer_2 (
    .out1(write1), .out2(write2), .out3(write3), .in(RD_WRITE_ENABLE), .sel(RD));  // open: out0, en
  Multiplexer #(.width(8)) multiplexer_6 (
    .in0(REG_1_VALUE), .in1(r1in), .out(multiplexer_6_out), .sel(write1));  // open: en
  Register Reg_1 (.D(multiplexer_6_out), .Q(REG_1_VALUE), .clk(clk));  // open: en, clr
  Multiplexer #(.width(8)) multiplexer_7 (
    .in0(multiplexer_4_out), .in1(multiplexer_5_out), .out(RT_READ_VALUE), .sel(RT[1]));  // open: en
  Multiplexer #(.width(8)) multiplexer_8 (
    .in0(REG_2_VALUE), .in1(r2in), .out(multiplexer_8_out), .sel(write2));  // open: en
  Register Reg_2 (.D(multiplexer_8_out), .Q(REG_2_VALUE), .clk(clk));  // open: en, clr
  Multiplexer #(.width(8)) multiplexer_9 (
    .in0(REG_3_VALUE), .in1(r3in), .out(multiplexer_9_out), .sel(write3));  // open: en
  Register Reg_3 (.D(multiplexer_9_out), .Q(REG_3_VALUE), .clk(clk));  // open: en, clr

  // Other names for the same wires on the sheet: r0[7:0] = REG_0_VALUE; r1[7:0] = REG_1_VALUE; r2[7:0] = REG_2_VALUE;
  //   r3[7:0] = REG_3_VALUE; rs_read[7:0] = RS_READ_VALUE; rt_read[7:0] = RT_READ_VALUE
endmodule
