// Logisim project cpu.circ as structural Verilog: 22 circuits, main circuit main
// CPU
module main (
  input  [31:0] RS_READ_VALUE,
  input  [31:0] RI_READ_VALUE,
  input  [31:0] RD_READ_VALUE,
  input  [31:0] JC_READ_VALUE,
  input  [31:0] INSTRUCTION,
  input  CLOCK,
  output [4:0] RS,
  output [4:0] RI,
  output [4:0] RD,
  output [31:0] RD_WRITE_VALUE,
  output RD_WRITE_ENABLE,
  output [23:0] FETCH_ADDRESS
);

  wire I, JUMP, WORD_MODE, WRITE;
  wire [1:0] u_control_1_write_value___00_for_load__01_for_alu_result__10_for_ra;
  wire [2:0] JC_t;
  wire [3:0] OP;
  wire [16:0] IMM;
  wire [23:0] ADDR, bit_extender_4_out, J_ADDR, multiplexer_2_out, ra;
  wire [24:0] bit_extender_2_out;
  wire [31:0] ALU_OUT, bit_extender_1_out, bit_extender_3_out, DATA_OUT, multiplexer_1_out;

  Multiplexer #(.width(32), .enable("false")) multiplexer_1 (
    .in0(RI_READ_VALUE), .in1(bit_extender_1_out), .out(multiplexer_1_out), .sel(I));
  assign bit_extender_1_out = {{15{IMM[16]}}, IMM};  // Bit_Extender bit_extender_1
  // Probe on multiplexer_1_out
  Multiplexer #(.width(24), .enable("false")) multiplexer_2 (
    .in0(ra), .in1(J_ADDR), .out(multiplexer_2_out), .sel(JUMP));
  u_ALU u_alu_1 (.ALU_X(RS_READ_VALUE), .ALU_RESULT(ALU_OUT), .ALU_Y(multiplexer_1_out), .ALU_CONTROL(OP));
  Bit_Extender #(.in_width(32), .out_width(25)) bit_extender_2 (.in(ALU_OUT), .out(bit_extender_2_out));
  u__1 u__1_1 (.Out(ra), .in_1(FETCH_ADDRESS));
  Register #(.width(24)) PC (.D(multiplexer_2_out), .Q(FETCH_ADDRESS), .clk(CLOCK));  // open: en, clr
  // Probe on ALU_OUT
  u_MEM u_mem_1 (
    .ADDRESS(bit_extender_2_out), .WORD_MODE(WORD_MODE), .MEM_WRITE(WRITE), .DATA_IN(RD_READ_VALUE),
    .CLOCK(CLOCK), .DATA_OUT(DATA_OUT));
  u_INST_DECODE u_inst_decode_1 (
    .Instruction_in(INSTRUCTION), .RD(RD), .RS(RS), .RI(RI), .IMM(IMM), .ADDR(ADDR), .OP(OP), .JC(JC_t),
    .TOGGLE(I));
  Multiplexer #(.width(24), .enable("false")) multiplexer_3 (
    .in0(bit_extender_4_out), .in1(ADDR), .out(J_ADDR), .sel(I));
  assign bit_extender_3_out = {{8{1'b0}}, ra};  // Bit_Extender bit_extender_3
  u_CONTROL u_control_1 (
    .WORD_MODE(WORD_MODE), .out_9(WRITE), .Jump(JUMP), .rd_write(RD_WRITE_ENABLE),
    .write_value___00_for_load__01_for_ALU_result__10_for_ra(u_control_1_write_value___00_for_load__01_for_alu_result__10_for_ra),
    .OP(OP), .toggle(I), .JC_2(JC_t), .JC(JC_READ_VALUE));
  Bit_Extender #(.in_width(32), .out_width(24)) bit_extender_4 (.in(RI_READ_VALUE), .out(bit_extender_4_out));
  Multiplexer #(.select(2), .width(32), .enable("false")) multiplexer_4 (
    .in0(DATA_OUT), .in1(ALU_OUT), .in2(bit_extender_3_out), .out(RD_WRITE_VALUE),
    .sel(u_control_1_write_value___00_for_load__01_for_alu_result__10_for_ra));  // open: in3
  // Probe on u_control_1_write_value___00_for_load__01_for_alu_result__10_for_ra

  // Other names for the same wires on the sheet: CLK = CLOCK; FETCH[23:0] = FETCH_ADDRESS; INST[31:0] = INSTRUCTION;
  //   JC[31:0] = JC_READ_VALUE; RD_t[31:0] = RD_READ_VALUE; RD_WE = RD_WRITE_ENABLE; RD_WV[31:0] = RD_WRITE_VALUE;
  //   RI_t[31:0] = RI_READ_VALUE; RS_t[31:0] = RS_READ_VALUE
endmodule

module u_ALU (
  input  [31:0] ALU_X,
  input  [31:0] ALU_Y,
  input  [3:0] ALU_CONTROL,
  output [31:0] ALU_RESULT
);

  wire [4:0] Y_prime;
  wire [31:0] ADD, AND, DIV, MUL, OR, REV, SL, SR, STU, SUB, XOR;

  Bit_Extender #(.in_width(32), .out_width(5)) bit_extender_1 (.in(ALU_Y), .out(Y_prime));
  u_SL u_sl_1 (.IN(ALU_X), .SHIFT(Y_prime), .OUT(SL));
  u_REV u_rev_1 (.INPUT(ALU_X), .OUTPUT(REV), .REVERSE_AMOUNT(Y_prime));
  Multiplier #(.width(32)) multiplier_1 (.a(ALU_X), .b(ALU_Y), .out(MUL));  // open: cin, cout
  Bit_Extender #(.in_width(32), .out_width(15)) bit_extender_2 (.in(ALU_X), .out(STU[14:0]));
  Bit_Extender #(.in_width(32), .out_width(17)) bit_extender_3 (.in(ALU_Y), .out(STU[31:15]));
  Shifter #(.width(32), .shift("ar")) shifter_1 (.in(ALU_X), .\dist (Y_prime), .out(SR));
  assign XOR = ALU_X ^ ALU_Y;  // XOR_Gate xor_1, 32 bits wide
  u_Signed_DIV u_signed_div_1 (.Input_1(ALU_X), .Input_2(ALU_Y), .out_3(DIV));
  assign AND = ALU_X & ALU_Y;  // AND_Gate and_1, 32 bits wide
  Adder #(.width(32)) adder_1 (.a(ALU_X), .b(ALU_Y), .out(ADD));  // open: cin, cout
  assign OR = ALU_X | ALU_Y;  // OR_Gate or_1, 32 bits wide
  Subtractor #(.width(32)) subtractor_1 (.a(ALU_X), .b(ALU_Y), .out(SUB));  // open: bin, bout
  Multiplexer #(.select(4), .width(32), .enable("false")) multiplexer_1 (
    .in0(SL), .in1(SR), .in2(AND), .in3(OR), .in4(REV), .in5(XOR), .in6(ADD), .in7(SUB), .in8(MUL),
    .in9(DIV), .in10(ADD), .in11(ADD), .in12(ADD), .in13(ADD), .in14(STU), .out(ALU_RESULT), .sel(ALU_CONTROL));  // open: in15

  // Other names for the same wires on the sheet: X[31:0] = ALU_X; Y[31:0] = ALU_Y

  // Notes on the sheet:
  //   Feel free to use this component, or not, however you want!
  //   Feel free to use this component, or not, however you want!
endmodule

// Data Memory
module u_MEM (
  input  [24:0] ADDRESS,
  input  WORD_MODE,
  input  MEM_WRITE,
  input  [31:0] DATA_IN,
  input  CLOCK,
  output [31:0] DATA_OUT
);

  wire evenLoad, evenWrite, not_3_out, oddLoad, oddWrite, or_1_out, or_2_out;
  wire [15:0] evenIN, evenread, HALFWORD_OUT, multiplexer_3_out, multiplexer_6_out, oddIN, oddread;
  wire [23:0] adder_1_out, address_even;
  wire [31:0] bit_extender_1_out, WORD_OUT;

  Multiplexer #(.width(24), .enable("false")) multiplexer_1 (
    .in0(ADDRESS[24:1]), .in1(adder_1_out), .out(address_even), .sel(ADDRESS[0]));
  Adder #(.width(24)) adder_1 (.a(ADDRESS[24:1]), .b(24'h1), .out(adder_1_out));  // open: cin, cout
  not not_1 (evenLoad, evenWrite);
  not not_2 (oddLoad, oddWrite);
  Multiplexer #(.width(16), .enable("false")) multiplexer_2 (
    .in0(evenread), .in1(oddread), .out(HALFWORD_OUT), .sel(ADDRESS[0]));
  // Probe on HALFWORD_OUT
  or or_1 (or_1_out, WORD_MODE, ADDRESS[0]);
  Multiplexer #(.width(16), .enable("false")) multiplexer_3 (
    .in0(DATA_IN[31:16]), .in1(DATA_IN[15:0]), .out(multiplexer_3_out), .sel(ADDRESS[0]));
  and and_1 (oddWrite, or_1_out, MEM_WRITE);
  Multiplexer #(.width(16), .enable("false")) multiplexer_4 (
    .in1(multiplexer_3_out), .out(oddIN), .sel(oddWrite));  // open: in0
  not not_3 (not_3_out, ADDRESS[0]);
  Multiplexer #(.width(32), .enable("false")) multiplexer_5 (
    .in0({oddread, evenread}), .in1({evenread, oddread}), .out(WORD_OUT), .sel(ADDRESS[0]));
  // Probe on WORD_OUT
  or or_2 (or_2_out, WORD_MODE, not_3_out);
  and and_2 (evenWrite, or_2_out, MEM_WRITE);
  Multiplexer #(.width(16), .enable("false")) multiplexer_6 (
    .in0(DATA_IN[15:0]), .in1(DATA_IN[31:16]), .out(multiplexer_6_out), .sel(ADDRESS[0]));
  RAM #(.addrWidth(24), .dataWidth(16)) ram_1 (
    .addr(address_even), .data(evenread), .clk(CLOCK), .ld(evenLoad));  // open: sel, clr
  RAM #(.addrWidth(24), .dataWidth(16)) ram_2 (
    .addr(ADDRESS[24:1]), .data(oddread), .clk(CLOCK), .ld(oddLoad));  // open: sel, clr
  Multiplexer #(.width(16), .enable("false")) multiplexer_7 (
    .in1(multiplexer_6_out), .out(evenIN), .sel(evenWrite));  // open: in0
  Multiplexer #(.width(16), .enable("false")) multiplexer_8 (
    .in1(evenIN), .out(evenread), .sel(evenWrite));  // open: in0
  Multiplexer #(.width(16), .enable("false")) multiplexer_9 (.in1(oddIN), .out(oddread), .sel(oddWrite));  // open: in0
  assign bit_extender_1_out = {{16{1'b0}}, HALFWORD_OUT};  // Bit_Extender bit_extender_1
  Multiplexer #(.width(32), .enable("false")) multiplexer_10 (
    .in0(bit_extender_1_out), .in1(WORD_OUT), .out(DATA_OUT), .sel(WORD_MODE));

  // Other names for the same wires on the sheet: odd = ADDRESS[0]; address_t[23:0] = ADDRESS[24:1]; CLK = CLOCK;
  //   lowerIN[15:0] = DATA_IN[15:0]; higherIN[15:0] = DATA_IN[31:16]; word = WORD_MODE; write = MEM_WRITE

  // Notes on the sheet:
  //   if odd addr requested
  //   even
  //   odd
  //   output
  //   Feel free to use this component, or not, however you want!
  //   You might use the word mode input to differentiate LW/SW from LH/SH.
  //   However, you *SHOULD* use 2 RAM modules, one for even addresses and one for odd addresses.
endmodule

module u_REV (
  input  [31:0] INPUT,
  input  [4:0] REVERSE_AMOUNT,
  output [31:0] OUTPUT
);

  wire [31:0] u_rev2_1_output, u_rev4_1_output, u_rev8_1_output, u_rev16_1_output;

  u_REV16 u_rev16_1 (.INPUT(INPUT), .ON(REVERSE_AMOUNT[4]), .OUTPUT(u_rev16_1_output));
  u_REV8 u_rev8_1 (.INPUT(u_rev16_1_output), .ON(REVERSE_AMOUNT[3]), .OUTPUT(u_rev8_1_output));
  u_REV1 u_rev1_1 (.INPUT(u_rev2_1_output), .ON(REVERSE_AMOUNT[0]), .OUTPUT(OUTPUT));
  u_REV2 u_rev2_1 (.INPUT(u_rev4_1_output), .ON(REVERSE_AMOUNT[1]), .OUTPUT(u_rev2_1_output));
  u_REV4 u_rev4_1 (.INPUT(u_rev8_1_output), .ON(REVERSE_AMOUNT[2]), .OUTPUT(u_rev4_1_output));

  // Notes on the sheet:
  //   Feel free to use this component, or not, however you want!
endmodule

module u_INST_DECODE (
  input  [31:0] Instruction_in,
  output [3:0] OP,
  output TOGGLE,
  output [2:0] JC,
  output [4:0] RD,
  output [4:0] RS,
  output [4:0] RI,
  output [16:0] IMM,
  output [23:0] ADDR
);

  wire JUMP, R_TYPE;
  wire [23:0] REST;

  Comparator #(.width(4)) comparator_1 (.a(OP), .b(4'b1111), .eq(R_TYPE));  // open: gt, lt
  u_INST_SPLIT u_inst_split_1 (
    .INST(Instruction_in), .OP_CODE(OP), .TOGGLE(TOGGLE), .REST({JC, REST[23:22], RS, REST[16:0]}));
  Comparator #(.width(4)) comparator_2 (.a(4'b1111), .b(OP), .eq(JUMP));  // open: gt, lt
  Bit_Extender #(.in_width(27), .out_width(5)) bit_extender_1 (.in({JC, REST[23:22], RS, REST[16:0]}), .out(RI));
  Bit_Extender #(.in_width(27), .out_width(17)) bit_extender_2 (.in({JC, REST[23:22], RS, REST[16:0]}), .out(IMM));
  Bit_Extender #(.in_width(27), .out_width(24)) bit_extender_3 (.in({JC, REST[23:22], RS, REST[16:0]}), .out(ADDR));
  Multiplexer #(.width(5), .enable("false")) multiplexer_1 (
    .in0({JC, REST[23:22]}), .in1(5'b00110), .out(RD), .sel(JUMP));

  // Other names for the same wires on the sheet: _27 = TOGGLE; REST (some bits) = {JC, RS}
endmodule

module u_INST_SPLIT (
  input  [31:0] INST,
  output [3:0] OP_CODE,
  output TOGGLE,
  output [26:0] REST
);


  assign OP_CODE = INST[31:28];
  assign REST = INST[26:0];
  assign TOGGLE = INST[27];
endmodule

module u_CONTROL (
  input  [31:0] JC,
  input  [3:0] OP,
  input  toggle,
  input  [2:0] JC_2,
  output Jump,
  output [1:0] write_value___00_for_load__01_for_ALU_result__10_for_ra,
  output rd_write,
  output WORD_MODE,
  output out_9
);

  wire and_1_out, comparator_2_eq, comparator_3_eq, comparator_5_eq, comparator_5_lt, comparator_6_eq,
       comparator_7_eq, comparator_9_eq, comparator_12_eq, comparator_12_gt, comparator_13_eq,
       comparator_14_eq, JAL, JEQ, JGE, JGT, JLE, JLT, JNE, or_4_out, or_6_out;

  or or_1 (WORD_MODE, comparator_2_eq, comparator_3_eq);
  Comparator #(.width(4)) comparator_1 (
    .a(4'b1111), .b(OP), .eq(write_value___00_for_load__01_for_ALU_result__10_for_ra[1]));  // open: gt, lt
  Comparator #(.width(4)) comparator_2 (.a(4'b1100), .b(OP), .eq(comparator_2_eq));  // open: gt, lt
  Comparator #(.width(4)) comparator_3 (.a(4'b1101), .b(OP), .eq(comparator_3_eq));  // open: gt, lt
  Comparator #(.width(32)) comparator_4 (.a(JC), .b({32{1'b0}}), .gt(JGT));  // open: eq, lt
  Comparator #(.width(32)) comparator_5 (
    .a(JC), .b({32{1'b0}}), .eq(comparator_5_eq), .lt(comparator_5_lt));  // open: gt
  Comparator #(.width(4)) comparator_6 (.a(4'b1101), .b(OP), .eq(comparator_6_eq));  // open: gt, lt
  Comparator #(.width(4)) comparator_7 (.a(4'b1011), .b(OP), .eq(comparator_7_eq));  // open: gt, lt
  Multiplexer #(.select(3), .disabled(0)) multiplexer_1 (
    .in0(1'b1), .in1(JGT), .in2(JEQ), .in3(JLT), .in4(JLE), .in5(JNE), .in6(JGE), .in7(1'b1), .out(Jump),
    .sel(JC_2), .en(write_value___00_for_load__01_for_ALU_result__10_for_ra[1]));
  or or_2 (JLE, comparator_5_eq, comparator_5_lt);
  or or_3 (out_9, comparator_6_eq, comparator_7_eq);
  Comparator #(.width(32)) comparator_8 (.a({32{1'b0}}), .b(JC), .eq(JEQ));  // open: gt, lt
  Comparator #(.width(32)) comparator_9 (.a(JC), .b({32{1'b0}}), .eq(comparator_9_eq));  // open: gt, lt
  not not_1 (JNE, comparator_9_eq);
  Comparator #(.width(3)) comparator_10 (.a(3'b111), .b(JC_2), .eq(JAL));  // open: gt, lt
  and and_1 (and_1_out, ~JAL, write_value___00_for_load__01_for_ALU_result__10_for_ra[1]);  // AND_Gate
  not not_2 (rd_write, or_4_out);
  or or_4 (or_4_out, and_1_out, out_9);
  Comparator #(.width(32)) comparator_11 (.a(JC), .b({32{1'b0}}), .lt(JLT));  // open: gt, eq
  Comparator #(.width(32)) comparator_12 (
    .a(JC), .b({32{1'b0}}), .gt(comparator_12_gt), .eq(comparator_12_eq));  // open: lt
  Comparator #(.width(4)) comparator_13 (.a(4'b1100), .b(OP), .eq(comparator_13_eq));  // open: gt, lt
  Comparator #(.width(4)) comparator_14 (.a(4'b1010), .b(OP), .eq(comparator_14_eq));  // open: gt, lt
  or or_5 (JGE, comparator_12_gt, comparator_12_eq);
  not not_3 (write_value___00_for_load__01_for_ALU_result__10_for_ra[0], or_6_out);
  or or_6 (or_6_out, comparator_13_eq, write_value___00_for_load__01_for_ALU_result__10_for_ra[1], comparator_14_eq);

  // Other names for the same wires on the sheet: I = toggle; JC_t[2:0] = JC_2; store = out_9;
  //   is_a_jump = write_value___00_for_load__01_for_ALU_result__10_for_ra[1]
endmodule

module u_SL (
  input  [31:0] IN,
  input  [4:0] SHIFT,
  output [31:0] OUT
);

  wire [31:0] u_sla2_1_out, u_sla4_1_out, u_sla8_1_out, u_sla16_1_out;

  u_SLA16 u_sla16_1 (.IN(IN), .ON(SHIFT[4]), .OUT(u_sla16_1_out));
  u_SLA4 u_sla4_1 (.IN(u_sla8_1_out), .ON(SHIFT[2]), .OUT(u_sla4_1_out));
  u_SLA8 u_sla8_1 (.IN(u_sla16_1_out), .ON(SHIFT[3]), .OUT(u_sla8_1_out));
  u_SLA2 u_sla2_1 (.IN(u_sla4_1_out), .ON(SHIFT[1]), .OUT(u_sla2_1_out));
  u_SLA1 u_sla1_1 (.IN(u_sla2_1_out), .ON(SHIFT[0]), .OUT(OUT));
endmodule

module u_SLA1 (
  input  [31:0] IN,
  input  ON,
  output [31:0] OUT
);

  wire [0:0] bit_extender_1_out;
  wire [30:0] bit_extender_2_out;

  Bit_Extender #(.in_width(32), .out_width(1)) bit_extender_1 (.in(IN), .out(bit_extender_1_out[0]));
  Bit_Extender #(.in_width(32), .out_width(31)) bit_extender_2 (.in(IN), .out(bit_extender_2_out));
  Multiplexer #(.width(32), .enable("false")) multiplexer_1 (
    .in0(IN), .in1({bit_extender_2_out, bit_extender_1_out[0]}), .out(OUT), .sel(ON));
endmodule

module u_SLA2 (
  input  [31:0] IN,
  input  ON,
  output [31:0] OUT
);

  wire [31:0] u_sla1_1_out;

  u_SLA1 u_sla1_1 (.IN(IN), .ON(ON), .OUT(u_sla1_1_out));
  u_SLA1 u_sla1_2 (.IN(u_sla1_1_out), .ON(ON), .OUT(OUT));
endmodule

module u_SLA4 (
  input  [31:0] IN,
  input  ON,
  output [31:0] OUT
);

  wire [31:0] u_sla2_1_out;

  u_SLA2 u_sla2_1 (.IN(IN), .ON(ON), .OUT(u_sla2_1_out));
  u_SLA2 u_sla2_2 (.IN(u_sla2_1_out), .ON(ON), .OUT(OUT));
endmodule

module u_SLA8 (
  input  [31:0] IN,
  input  ON,
  output [31:0] OUT
);

  wire [31:0] u_sla4_1_out;

  u_SLA4 u_sla4_1 (.IN(IN), .ON(ON), .OUT(u_sla4_1_out));
  u_SLA4 u_sla4_2 (.IN(u_sla4_1_out), .ON(ON), .OUT(OUT));
endmodule

module u_SLA16 (
  input  [31:0] IN,
  input  ON,
  output [31:0] OUT
);

  wire [31:0] u_sla8_1_out;

  u_SLA8 u_sla8_1 (.IN(IN), .ON(ON), .OUT(u_sla8_1_out));
  u_SLA8 u_sla8_2 (.IN(u_sla8_1_out), .ON(ON), .OUT(OUT));
endmodule

module u_SLA32 (
  input  [31:0] IN,
  input  ON,
  output [31:0] OUT
);

  wire [31:0] u_sla16_1_out;

  u_SLA16 u_sla16_1 (.IN(IN), .ON(ON), .OUT(u_sla16_1_out));
  u_SLA16 u_sla16_2 (.IN(u_sla16_1_out), .ON(ON), .OUT(OUT));
endmodule

module u_Signed_DIV (
  input  [31:0] Input_1,
  input  [31:0] Input_2,
  output [31:0] out_3
);

  wire comparator_2_gt, comparator_2_lt, eq, gt, lt, nonzero;
  wire [31:0] multiplexer_1_out, u_ext_div_1_output, zero_result;

  Multiplexer #(.width(32)) multiplexer_1 (
    .in0({32{1'b0}}), .in1(32'h80000000), .out(multiplexer_1_out), .sel(lt));  // open: en
  Comparator #(.width(32)) comparator_1 (.a(Input_1), .b({32{1'b0}}), .gt(gt), .eq(eq), .lt(lt));
  Comparator #(.width(32)) comparator_2 (
    .a(Input_2), .b({32{1'b0}}), .gt(comparator_2_gt), .lt(comparator_2_lt));  // open: eq
  u_ext_DIV u_ext_div_1 (.INPUT_1(Input_1), .INPUT_2(Input_2), .OUTPUT(u_ext_div_1_output));
  Multiplexer #(.width(32)) multiplexer_2 (
    .in0(multiplexer_1_out), .in1(32'h7fffffff), .out(zero_result), .sel(gt));  // open: en
  Multiplexer #(.width(32)) multiplexer_3 (
    .in0(zero_result), .in1(u_ext_div_1_output), .out(out_3), .sel(nonzero));  // open: en
  or or_1 (nonzero, comparator_2_gt, comparator_2_lt);

  // Other names for the same wires on the sheet: In_1[31:0] = Input_1; In_2[31:0] = Input_2
endmodule

module u_REV1 (
  input  [31:0] INPUT,
  input  ON,
  output [31:0] OUTPUT
);

  Multiplexer #(.width(32), .enable("false")) multiplexer_1 (
    .in0(INPUT),
    .in1({INPUT[30], INPUT[31], INPUT[28], INPUT[29], INPUT[26], INPUT[27], INPUT[24], INPUT[25], INPUT[22], INPUT[23], INPUT[20], INPUT[21], INPUT[18], INPUT[19], INPUT[16], INPUT[17], INPUT[14], INPUT[15], INPUT[12], INPUT[13], INPUT[10], INPUT[11], INPUT[8], INPUT[9], INPUT[6], INPUT[7], INPUT[4], INPUT[5], INPUT[2], INPUT[3], INPUT[0], INPUT[1]}),
    .out(OUTPUT), .sel(ON));
endmodule

module u_REV2 (
  input  [31:0] INPUT,
  input  ON,
  output [31:0] OUTPUT
);

  Multiplexer #(.width(32), .enable("false")) multiplexer_1 (
    .in0(INPUT),
    .in1({INPUT[29:28], INPUT[31:30], INPUT[25:24], INPUT[27:26], INPUT[21:20], INPUT[23:22], INPUT[17:16], INPUT[19:18], INPUT[13:12], INPUT[15:14], INPUT[9:8], INPUT[11:10], INPUT[5:4], INPUT[7:6], INPUT[1:0], INPUT[3:2]}),
    .out(OUTPUT), .sel(ON));
endmodule

module u_REV4 (
  input  [31:0] INPUT,
  input  ON,
  output [31:0] OUTPUT
);

  Multiplexer #(.width(32), .enable("false")) multiplexer_1 (
    .in0(INPUT),
    .in1({INPUT[27:24], INPUT[31:28], INPUT[19:16], INPUT[23:20], INPUT[11:8], INPUT[15:12], INPUT[3:0], INPUT[7:4]}),
    .out(OUTPUT), .sel(ON));
endmodule

module u_REV8 (
  input  [31:0] INPUT,
  input  ON,
  output [31:0] OUTPUT
);

  Multiplexer #(.width(32), .enable("false")) multiplexer_1 (
    .in0(INPUT), .in1({INPUT[23:16], INPUT[31:24], INPUT[7:0], INPUT[15:8]}), .out(OUTPUT), .sel(ON));
endmodule

module u_REV16 (
  input  [31:0] INPUT,
  input  ON,
  output [31:0] OUTPUT
);

  Multiplexer #(.width(32), .disabled(0), .enable("false")) multiplexer_1 (
    .in0(INPUT), .in1({INPUT[15:0], INPUT[31:16]}), .out(OUTPUT), .sel(ON));
endmodule

module u__1 (
  input  [23:0] in_1,
  output [23:0] Out
);

  Adder #(.width(24)) adder_1 (.a(24'h1), .b(in_1), .out(Out));  // open: cin, cout
endmodule

module u_ext_DIV (
  input  [31:0] INPUT_1,
  input  [31:0] INPUT_2,
  output [31:0] OUTPUT
);

  wire x_0, y_0;
  wire [31:0] minus_x, minus_x__y, minus_x_y, minus_y, multiplexer_1_out, multiplexer_2_out, negator_3_out,
       negator_4_out, x__y, x_y;

  // Probe on INPUT_1
  // Probe on INPUT_2
  Negator #(.width(32)) negator_1 (.in(INPUT_1), .out(minus_x));
  Negator #(.width(32)) negator_2 (.in(INPUT_2), .out(minus_y));
  Negator #(.width(32)) negator_3 (.in(minus_x_y), .out(negator_3_out));
  Negator #(.width(32)) negator_4 (.in(x__y), .out(negator_4_out));
  Multiplexer #(.width(32)) multiplexer_1 (
    .in0(minus_x__y), .in1(negator_3_out), .out(multiplexer_1_out), .sel(y_0));  // open: en
  Multiplexer #(.width(32)) multiplexer_2 (
    .in0(negator_4_out), .in1(x_y), .out(multiplexer_2_out), .sel(y_0));  // open: en
  Comparator #(.width(32)) comparator_1 (.a(INPUT_1), .b({32{1'b0}}), .gt(x_0));  // open: eq, lt
  Comparator #(.width(32)) comparator_2 (.a(INPUT_2), .b({32{1'b0}}), .gt(y_0));  // open: eq, lt
  Multiplexer #(.width(32)) multiplexer_3 (
    .in0(multiplexer_1_out), .in1(multiplexer_2_out), .out(OUTPUT), .sel(x_0));  // open: en
  // Probe on OUTPUT
  Divider #(.width(32)) divider_1 (.a(INPUT_1), .b(INPUT_2), .out(x_y));  // open: upper, rem
  Divider #(.width(32)) divider_2 (.a(minus_x), .b(INPUT_2), .out(minus_x_y));  // open: upper, rem
  Divider #(.width(32)) divider_3 (.a(INPUT_1), .b(minus_y), .out(x__y));  // open: upper, rem
  Divider #(.width(32)) divider_4 (.a(minus_x), .b(minus_y), .out(minus_x__y));  // open: upper, rem

  // Other names for the same wires on the sheet: x[31:0] = INPUT_1; y[31:0] = INPUT_2
endmodule
